# Fritzing sketch LinkSensorProcess (saved by Fritzing 0.9.4)

parts:
  Bauteil1 = Arduino Pro Mini V2 (5V)
  U1 = WS2812 RGB LED strip
  R1 = Resistor [tolerance=±5% resistance=1M package="2010 [SMD]"]
  VCC1 = Battery block 9V
  C1 = Film/Foil Capacitor [capacitance=100nF voltage=35V package="5mm [THT, pp]"]
  U2 = WS2812 RGB LED strip
  U3 = WS2812 RGB LED strip
  C2 = Film/Foil Capacitor [capacitance=100nF voltage=35V package="5mm [THT, pp]"]
  R2 = Resistor [tolerance=±5% resistance=1M package="2010 [SMD]"]
  C3 = Film/Foil Capacitor [capacitance=100nF voltage=35V package="5mm [THT, pp]"]
  R3 = Resistor [tolerance=±5% resistance=1M package="2010 [SMD]"]

nets:
  VCC: Bauteil1.VCC, U1.VCC, U2.VCC, U3.VCC
  GND: Bauteil1.GND, U1.GND, VCC1.-, U2.GND, U3.GND
  N1: Bauteil1.RAW, VCC1.+
  N2: Bauteil1.D10, C3.+, R3.Pin_1
  N3: Bauteil1.D9, R3.Pin_0
  N4: Bauteil1.D8, Bauteil1.D6, R1.Pin_1, C1.-, C2.+, R2.Pin_1
  N5: Bauteil1.D7, R2.Pin_0
  N6: Bauteil1.D5, R1.Pin_0
  N7: Bauteil1.D4, U3.DIN
  N8: Bauteil1.D3, U2.DIN
  N9: Bauteil1.D2, U1.DIN

custom parts:
  Arduino Pro Mini V2 (5V): Arduino Pro Mini V2 There are several different layouts for this board out there. This one is modeled after the Sparkfun 11113 board but a few of the pins have been moved around.
  WS2812 RGB LED strip: WS2812 strip
